// Logisim project compsystems.circ as structural Verilog
module compsystems_circ (
  input  P2,
  input  P1,
  input  P0,
  input  U,
  output N2,
  output N1,
  output N0
);

  wire and_1_out, and_2_out, and_3_out, and_4_out, and_5_out, and_6_out, and_7_out, and_8_out, and_9_out,
       and_10_out, not_1_out, not_2_out, not_3_out, not_4_out, not_5_out, not_6_out, not_7_out, not_8_out,
       not_9_out, not_10_out, not_11_out, not_12_out, not_13_out, not_14_out, not_15_out, not_16_out;

  not not_1 (not_1_out, P2);
  not not_2 (not_2_out, P0);
  not not_3 (not_3_out, P1);
  not not_4 (not_4_out, P0);
  not not_5 (not_5_out, U);
  not not_6 (not_6_out, P1);
  and and_1 (and_1_out, not_6_out, P0, U);
  and and_2 (and_2_out, P1, not_7_out);
  not not_7 (not_7_out, U);
  and and_3 (and_3_out, P2, not_8_out, U);
  not not_8 (not_8_out, P1);
  not not_9 (not_9_out, P2);
  not not_10 (not_10_out, P1);
  not not_11 (not_11_out, P0);
  not not_12 (not_12_out, U);
  not not_13 (not_13_out, P2);
  not not_14 (not_14_out, U);
  not not_15 (not_15_out, P1);
  not not_16 (not_16_out, U);
  and and_4 (and_4_out, not_1_out, P1, not_2_out, U);
  and and_5 (and_5_out, P2, not_3_out, not_4_out);
  or or_1 (N2, and_4_out, and_5_out, and_6_out);
  and and_6 (and_6_out, P2, not_5_out);
  or or_2 (N1, and_1_out, and_2_out, and_3_out);
  and and_7 (and_7_out, not_9_out, not_10_out, not_11_out, U);
  and and_8 (and_8_out, P0, not_12_out);
  and and_9 (and_9_out, not_13_out, P1, not_14_out);
  and and_10 (and_10_out, P2, not_15_out, not_16_out);
  or or_3 (N0, and_7_out, and_8_out, and_9_out, and_10_out);
endmodule
